# Fritzing sketch sketch_accorduino (saved by Fritzing 1.0.5)
circuit board: 19cm x 19cm
breadboards: 1

parts:
  Part1 = Arduino Pro Micro (Clone)
  Part2 = MPR121 Breakout
  Part3 = MPR121 Breakout
  Part4 = MPR121 Breakout
  Part5 = MPR121 Breakout

nets:
  GND: Part1.GND, Part2.GND, Part3.GND, Part4.GND, Part5.GND
  N1: Part1.D2, Part2.SDA, Part3.SDA, Part4.ADDR, Part4.SDA, Part5.SDA
  N2: Part1.D3, Part2.SCL, Part3.SCL, Part4.SCL, Part5.ADDR, Part5.SCL
  3.3V: Part1.VCC, Part2.ADDR, Part2.3.3V, Part3.3.3V, Part4.3.3V, Part5.3.3V
